// Digital circuit Multiplexers.dig as structural Verilog
module Multiplexers (
  input  in_1,
  input  in_2,
  input  in_3
);

  wire and_1_out, and_2_out, not_1_out, or_1_out;

  and and_1 (and_1_out, in_1, not_1_out);
  and and_2 (and_2_out, in_2, in_3);
  not not_1 (not_1_out, in_3);
  or or_1 (or_1_out, and_1_out, and_2_out);
  LED led_1 (.in(or_1_out));
endmodule
