// Digital circuit RS-trigger.dig as structural Verilog
module RS_trigger (
  input  in_1,
  input  in_2
);

  wire nor_1_out, nor_2_out;

  LED led_1 (.in(nor_1_out));
  nor nor_1 (nor_1_out, in_1, nor_2_out);
  LED led_2 (.in(nor_2_out));
  nor nor_2 (nor_2_out, nor_1_out, in_2);
endmodule
