// Digital circuit Sumator.dig as structural Verilog
module Sumator (
  input  in_1,
  input  in_2
);

  wire and_2_out, or_1_out, undriven, xor_1_out, xor_2_out;

  xor xor_1 (xor_1_out, in_1, in_2);
  LED led_1 (.in(or_1_out));
  LED led_2 (.in(xor_2_out));
  xor xor_2 (xor_2_out, xor_1_out, 1'b0);
  or or_1 (or_1_out, undriven, and_2_out);
  // And and_1 has open pins: In_1=1'b0, In_2=xor_1_out, out=open
  and and_2 (and_2_out, in_2, in_1);
endmodule
